# Fritzing sketch power (saved by Fritzing 0.9.2b)
circuit board: 8.05128cm x 8.4728cm

parts:
  10A = FUSE [package=fuse_5mm]
  5A = FUSE [package=fuse_5mm]
  5A_2 = FUSE [package=fuse_5mm]
  2A = FUSE [package=fuse_5mm]
  2A_2 = FUSE [package=fuse_5mm]
  2A_3 = FUSE [package=fuse_5mm]
  2A_4 = FUSE [package=fuse_5mm]
  2A_5 = FUSE [package=fuse_5mm]
  2A_6 = FUSE [package=fuse_5mm]
  2A_7 = FUSE [package=fuse_5mm]
  2A_8 = FUSE [package=fuse_5mm]
  2A_9 = FUSE [package=fuse_5mm]
  2A_10 = FUSE [package=fuse_5mm]

nets:
  N1: 10A.1, 2A.2, 2A_2.2, 2A_3.2, 2A_4.2
  12V: 10A.2, 5A.2, 5A_2.2
  N2: 5A.1, 2A_5.2, 2A_6.2, 2A_7.2
  N3: 5A_2.1, 2A_8.2, 2A_9.2, 2A_10.2
  5̅: 2A.1
  3: 2A_2.1
  2: 2A_3.1
  1̅: 2A_4.1
  3̅: 2A_5.1
  4: 2A_6.1
  5: 2A_7.1
  1: 2A_8.1
  4̅: 2A_9.1
  2̅: 2A_10.1
